# Fritzing sketch semaforo (saved by Fritzing 0.8.5b)

parts:
  LED1 = LED - 5mm [color="Red (633nm)" package="5 mm [THT]"]
  LED2 = LED - 5mm [color="Red (633nm)" package="5 mm [THT]"]
  LED3 = LED - 5mm [color="Red (633nm)" package="5 mm [THT]"]
  Componente1 = Arduino Leonardo (Rev3b)

nets:
  N1: LED1.anode, Componente1.D11_PWM
  N2: LED2.cathode, Componente1.D10_PWM/A10
  N3: LED2.anode, Componente1.D13_PWM
  N4: LED3.anode, Componente1.D12/A11
